# Fritzing sketch sketch (saved by Fritzing 0.8.3b)
breadboards: 1

parts:
  R1 = Resistor [tolerance=±5% resistance=100k package=THT]
  Part1 = Arduino Uno (Rev3)
  J1 = Piezo Speaker
  S1 = Textile Pushbutton
  LED1 = LED - 5mm [color="Red (633nm)" package="5 mm [THT]"]
  R2 = Resistor [tolerance=±5% resistance=100 package=THT]

nets:
  N1: R1.Pin_0, Part1.GND, J1.pin2, LED1.cathode
  N2: R1.Pin_1, Part1.A0, S1.leg1
  N3: Part1.ICSP_MISO, Part1.D12/MISO, LED1.anode
  N4: Part1.D7, R2.Pin_0
  N5: Part1.5V, S1.leg0
  N6: J1.pin1, R2.Pin_1
